// Logisim project Contador Assincrono Clear 0 a 9.circ as structural Verilog: 1 circuit, main circuit main
module main (
  input  in_1
);

  wire and_1_out, clock_1_out, t_ff_1_q, t_ff_2_q, t_ff_3_q, t_ff_4_q;

  and and_1 (and_1_out, t_ff_4_q, t_ff_2_q);
  Clock clock_1 (.out(clock_1_out));
  T_Flip_Flop #(.trigger("falling")) t_ff_1 (
    .clk(clock_1_out), .T(in_1), .Q(t_ff_1_q), .reset(and_1_out));  // open: Qn, preset, en
  T_Flip_Flop #(.trigger("falling")) t_ff_2 (
    .clk(t_ff_1_q), .T(in_1), .Q(t_ff_2_q), .reset(and_1_out));  // open: Qn, preset, en
  T_Flip_Flop #(.trigger("falling")) t_ff_3 (
    .clk(t_ff_2_q), .T(in_1), .Q(t_ff_3_q), .reset(and_1_out));  // open: Qn, preset, en
  T_Flip_Flop #(.trigger("falling")) t_ff_4 (
    .clk(t_ff_3_q), .T(in_1), .Q(t_ff_4_q), .reset(and_1_out));  // open: Qn, preset, en
endmodule
