// Logisim project Contador Assincrono Preset 15 a 5.circ as structural Verilog: 1 circuit, main circuit main
module main (
  input  in_1
);

  wire and_1_out, clock_1_out, not_1_out, not_2_out, not_3_out, not_4_out, t_ff_1_q, t_ff_1_qn, t_ff_2_q,
       t_ff_2_qn, t_ff_3_q, t_ff_3_qn, t_ff_4_q;

  not not_1 (not_1_out, t_ff_1_q);
  not not_2 (not_2_out, t_ff_4_q);
  not not_3 (not_3_out, t_ff_2_q);
  not not_4 (not_4_out, clock_1_out);
  Clock clock_1 (.out(clock_1_out));
  and and_1 (and_1_out, t_ff_3_q, not_2_out, not_3_out, not_1_out);
  T_Flip_Flop t_ff_1 (.clk(not_4_out), .T(in_1), .Q(t_ff_1_q), .Qn(t_ff_1_qn), .preset(and_1_out));  // open: reset, en
  T_Flip_Flop #(.trigger("falling")) t_ff_2 (
    .clk(t_ff_1_qn), .T(in_1), .Q(t_ff_2_q), .Qn(t_ff_2_qn), .preset(and_1_out));  // open: reset, en
  T_Flip_Flop #(.trigger("falling")) t_ff_3 (
    .clk(t_ff_2_qn), .T(in_1), .Q(t_ff_3_q), .Qn(t_ff_3_qn), .preset(and_1_out));  // open: reset, en
  T_Flip_Flop #(.trigger("falling")) t_ff_4 (
    .clk(t_ff_3_qn), .T(in_1), .Q(t_ff_4_q), .preset(and_1_out));  // open: Qn, reset, en
endmodule
