// Logisim project Contador Sincrono Sequencia 0-3-1-4-7-0.circ as structural Verilog: 1 circuit, main circuit main
module main (
);

  wire and_1_out, and_2_out, and_3_out, and_4_out, and_5_out, and_6_out, clock_1_out, d_ff_1_q, d_ff_1_qn,
       d_ff_2_q, d_ff_2_qn, d_ff_3_q, d_ff_3_qn, or_1_out, or_2_out, or_3_out;

  Clock clock_1 (.out(clock_1_out));
  or or_1 (or_1_out, and_1_out, and_4_out);
  and and_1 (and_1_out, d_ff_3_q, d_ff_2_qn, d_ff_1_qn);
  and and_2 (and_2_out, d_ff_1_q, d_ff_3_qn, d_ff_2_qn);
  D_Flip_Flop d_ff_1 (.clk(clock_1_out), .D(or_1_out), .Q(d_ff_1_q), .Qn(d_ff_1_qn));  // open: preset, en, reset
  D_Flip_Flop d_ff_2 (.clk(clock_1_out), .D(or_2_out), .Q(d_ff_2_q), .Qn(d_ff_2_qn));  // open: preset, en, reset
  or or_2 (or_2_out, and_2_out, and_3_out);
  and and_3 (and_3_out, d_ff_1_qn, d_ff_3_qn, d_ff_2_qn);
  D_Flip_Flop d_ff_3 (.clk(clock_1_out), .D(or_3_out), .Q(d_ff_3_q), .Qn(d_ff_3_qn));  // open: preset, en, reset
  or or_3 (or_3_out, and_5_out, and_6_out);
  and and_4 (and_4_out, d_ff_2_qn, d_ff_1_q, d_ff_3_qn);
  and and_5 (and_5_out, d_ff_2_qn, d_ff_3_qn);
  and and_6 (and_6_out, d_ff_1_qn, d_ff_3_q, d_ff_2_q);
endmodule
